# Fritzing sketch SPPOM Fritzing (saved by Fritzing 0.9.3b)
breadboards: 1

parts:
  DHT1 = DHT22 Humidity and Temperature Sensor
  U2 = ESP8266 NodeMCU LoLin module
  microSD1 = MicroSD Card Module
  Part3 = VEML7700 [part_number="Adafruit #4162"]
  M4 = pcf8574 io expansion board [package=THT]
  ZS-042_RTC1 = ZS-042 RTC Module  # not connected
  J2 = Basic Servo
  J1 = Basic Servo
  U3 = MPU 9250 Breakout [package="SIP (Single Inline) [THT]"]
  LED1 = LED - 5mm [color="Green (555nm)" package="5 mm [THT]"]
  LED2 = LED - 5mm [color="Green (555nm)" package="5 mm [THT]"]
  LED3 = LED - 5mm [color="Green (555nm)" package="5 mm [THT]"]
  LED4 = LED - 5mm [color="Green (555nm)" package="5 mm [THT]"]
  LED5 = LED - 5mm [color="Green (555nm)" package="5 mm [THT]"]
  LED6 = LED - 5mm [color="Green (555nm)" package="5 mm [THT]"]
  LED7 = LED - 5mm [color="Green (555nm)" package="5 mm [THT]"]
  R3 = Resistor [tolerance=±5% resistance=220 power=0.25W package=THT]
  R4 = Resistor [tolerance=±5% resistance=220 power=0.25W package=THT]
  R5 = Resistor [tolerance=±5% resistance=220 power=0.25W package=THT]
  R6 = Resistor [tolerance=±5% resistance=220 power=0.25W package=THT]
  R7 = Resistor [tolerance=±5% resistance=220 power=0.25W package=THT]
  R8 = Resistor [tolerance=±5% resistance=220 power=0.25W package=THT]
  R9 = Resistor [tolerance=±5% resistance=220 power=0.25W package=THT]
  LED8 = LED - 5mm [color="Red (635nm)" package="5 mm [THT]"]
  R10 = Resistor [tolerance=±5% resistance=220 power=0.25W package=THT]
  BAT2 = 18650 battery holder [package=battery-18650-kit]
  TP1 = TP4056 [chip_label=TP4056 package="DIP (Dual Inline) [THT]"]
  Part4 = Solar Cell
  INA3 = INA219 DC Current Sensor Breakout
  R11 = Resistor [tolerance=±5% resistance=22 power=1 package=THT]
  R12 = Resistor [tolerance=±5% resistance=22 power=1 package=THT]
  Boost_Convertor1 = Boost Convertor [part_number=XL6009E1 package=THT]
  F1 = FUSE [package=fuse_5mm]
  S1 = Toggle Switch [package=THT]
  U4 = Voltage Regulator - 5V [package="TO220 [THT]"]
  C2 = Electrolytic Capacitor [capacitance=10µF voltage=16V package="100 mil [THT, electrolytic]"]
  C5 = Electrolytic Capacitor [capacitance=0.22mF voltage=25V package="100 mil [THT, electrolytic]"]

nets:
  VCC: DHT1.VDD, microSD1.VCC, Part3.VIN, M4.VCC, J2.vcc, J1.vcc, U3.VCC, U3.AD0, LED1.anode, INA3.VCC, U4.output_voltage, C2.+
  N1: DHT1.DATA, U2.D3
  GND: DHT1.GND, U2.GND, microSD1.GND, Part3.GND, M4.GND, J2.gnd, J1.gnd, U3.GND, INA3.GND, R12.Pin_0, Boost_Convertor1.Negative_Output, U4.GND, C2.-, C5.-
  N2: U2.D0, J1.pulse
  N3: U2.D1, Part3.SCL, M4.SCL, U3.SCL, INA3.SCL
  N4: U2.D2, Part3.SDA, M4.SDA, U3.SDA, INA3.SDA
  N5: U2.D4, J2.pulse
  N6: U2.D5, microSD1.SCK
  N7: U2.D6, microSD1.MISO
  N8: U2.D7, microSD1.MOSI
  N9: U2.D8, microSD1.CS
  N10: M4.O0, R3.Pin_0
  N11: M4.O1, R4.Pin_0
  N12: M4.O3, R6.Pin_0
  N13: M4.O4, R7.Pin_0
  N14: M4.O5, R8.Pin_0
  N15: M4.O6, R9.Pin_0
  N16: M4.O7, R10.Pin_0
  N17: LED1.cathode, R3.Pin_1
  N18: LED2.cathode, R4.Pin_1
  N19: LED3.cathode, R5.Pin_1
  N20: LED4.cathode, R6.Pin_1
  N21: LED5.cathode, R7.Pin_1
  N22: LED6.cathode, R8.Pin_1
  N23: LED7.cathode, R9.Pin_1
  N24: LED8.cathode, R10.Pin_1
  N25: BAT2.+, S1.COM
  N26: BAT2.-, TP1.pin4
  N27: TP1.pin3, Boost_Convertor1.Positive_Input
  N28: TP1.pin5, S1.L1
  N29: TP1.pin6, Boost_Convertor1.Negative_Input
  N30: Part4.+, INA3.Vin+
  N31: INA3.Vin-, R11.Pin_1
  N32: R11.Pin_0, R12.Pin_1
  N33: Boost_Convertor1.Positive_Output, F1.1
  N34: F1.2, U4.input_voltage, C5.+

custom parts:
  ESP8266 NodeMCU LoLin module: ESP8266 based NodeMCU
  pcf8574 io expansion board: pcf8574 io expansion board.
  MPU 9250 Breakout: Generic MPU 9250 Breakout Board
  18650 battery holder: 18650 Battery
  TP4056: A DIP stand-in part for whatever IC you want. With 6 pins on a 300mil dual inline package (DIP) footprint.
  INA219 DC Current Sensor Breakout: INA DC Current Sensor Breakout
  Boost Convertor: DC to DC boost convertor
